# Fritzing sketch thingscon-example (saved by Fritzing 0.9.3b)
breadboards: 1

parts:
  Part1 = Arduino MKR1000
  LED1 = RGB LED (com. anode, rbg) [package="5 mm [THT]"]
  R1 = Photocell (LDR) [package=THT]
  R2 = Photocell (LDR) [package=THT]
  R3 = Resistor [tolerance=±5% resistance=220 package=THT]
  R4 = Resistor [tolerance=±5% resistance=220 package=THT]
  R5 = Resistor [tolerance=±5% resistance=220 package=THT]
  R6 = Resistor [tolerance=±5% resistance=220 package=THT]
  R7 = Resistor [tolerance=±5% resistance=220 package=THT]

nets:
  N1: Part1.A1, R2.pin_1, R4.Pin_0
  N2: Part1.A2, R1.pin_1, R3.Pin_0
  N3: Part1.D2_PWM, R5.Pin_1
  N4: Part1.D3_PWM, R6.Pin_1
  N5: Part1.D4_PWM, R7.Pin_1
  N6: Part1.GND, LED1.blue_cathode, R3.Pin_1, R4.Pin_1
  N7: Part1.5V, R1.pin_0, R2.pin_0
  N8: LED1.red_cathode, R5.Pin_0
  N9: LED1.common_anode, R6.Pin_0
  N10: LED1.green_cathode, R7.Pin_0

custom parts:
  Arduino MKR1000: MKR1000 is a powerful board that combines the functionality of the Zero and the Wi-Fi Shield. It is the ideal solution for makers wanting to design IoT projects with minimal previous experience in networking
